// Logisim project pritam.circ as structural Verilog: 19 circuits, main circuit main
module main (
  input  Reset
);

  wire and_1_out, Clock_out, nor_1_out, not_1_out;
  wire [1:0] imem_1_p2, Stat_q;
  wire [31:0] PC_q, PChold_q;

  and and_1 (and_1_out, Clock_out, nor_1_out);
  Clock Clock (.out(Clock_out));
  Register #(.width(32)) PC (.D(PChold_q), .Q(PC_q), .clk(and_1_out), .clr(Reset));  // open: en
  nor nor_1 (nor_1_out, Stat_q[1], Stat_q[0]);
  not not_1 (not_1_out, and_1_out);
  Register #(.width(2)) Stat (.D(imem_1_p2), .Q(Stat_q), .clk(not_1_out));  // open: en, clr
  // imem imem_1: pin names not known; wires that end beside it: PC_q, imem_1_p2
  Register #(.width(32)) PChold (.Q(PChold_q), .clk(not_1_out), .clr(Reset));  // open: D, en
endmodule

module Align (
  input  [7:0] B1,
  input  [7:0] B2,
  input  [7:0] B3,
  input  [7:0] B4,
  input  [7:0] B5,
  input  [7:0] B6,
  input  [7:0] B7,
  input  [7:0] B8,
  input  NeedRegs,
  input  [7:0] B9,
  output [3:0] rA,
  output [3:0] rB,
  output [31:0] valC_0,
  output [31:0] valC_1
);

  Multiplexer #(.width(32), .enable("false")) multiplexer_1 (
    .in0({B4, B3, B2, B1}), .in1({B5, B4, B3, B2}), .out(valC_0), .sel(NeedRegs));
  Multiplexer #(.width(32), .enable("false")) multiplexer_2 (
    .in0({B8, B7, B6, B5}), .in1({B9, B8, B7, B6}), .out(valC_1), .sel(NeedRegs));

  assign rA = B1[3:0];
  assign rB = B1[7:4];
endmodule

module Fetch (
  input  [7:0] in_1,
  input  [7:0] in_2,
  input  [7:0] in_3,
  input  [7:0] in_4,
  input  [7:0] in_5,
  input  [7:0] in_6,
  input  [7:0] in_7,
  input  [7:0] in_8,
  input  [7:0] in_9,
  input  [7:0] in_10,
  output [3:0] out_11,
  output [3:0] out_12
);

  wire needreg_1_needreg;

  needReg needreg_1 (.icode(in_1[3:0]), .needReg(needreg_1_needreg));
  Align align_1 (
    .B1(in_2), .B2(in_3), .B3(in_4), .B4(in_5), .B5(in_6), .B6(in_7), .B7(in_8), .B8(in_9), .B9(in_10),
    .NeedRegs(needreg_1_needreg));  // open: rA, rB, valC_0, valC_1

  assign out_11 = in_1[3:0];
  assign out_12 = in_1[7:4];
endmodule

module needReg (
  input  [3:0] icode,
  output needReg
);

  Multiplexer #(.select(4), .enable("false")) multiplexer_1 (
    .in0(1'b0), .in1(1'b0), .in2(1'b1), .in3(1'b1), .in4(1'b1), .in5(1'b1), .in6(1'b1), .in7(1'b0),
    .in8(1'b0), .in9(1'b0), .in10(1'b1), .in11(1'b1), .out(needReg), .sel(icode));  // open: in12, in13, in14, in15
endmodule

module needValC (
  input  [3:0] icode,
  output needsValC
);

  Multiplexer #(.select(4), .enable("false")) multiplexer_1 (
    .in0(1'b0), .in1(1'b0), .in2(1'b0), .in3(1'b0), .in4(1'b1), .in5(1'b1), .in6(1'b1), .in7(1'b0),
    .in8(1'b1), .in9(1'b1), .in10(1'b0), .in11(1'b0), .in12(1'b0), .out(needsValC), .sel(icode));  // open: in13, in14, in15
endmodule

module Execute (
  input  [31:0] A_0,
  input  [31:0] C_0,
  input  [31:0] A_1,
  input  [31:0] C_1,
  input  [31:0] B_0,
  input  [31:0] B_1,
  input  [3:0] Icode,
  input  [3:0] ifun,
  output Cond,
  output [31:0] valE_0,
  output [31:0] valE_1
);

  wire condcode_1_of, condcode_1_sf, condcode_1_zf, n64bitalu_1_of, n64bitalu_1_sf, n64bitalu_1_zf,
       setcc_1_out_2;
  wire [3:0] alufun_1_ifunout, checkjm_1_output;
  wire [31:0] alua_1_alua_0, alua_1_alua_1, alub_1_alub_0, alub_1_alub_1;

  aluA alua_1 (
    .valA0(A_0), .valC0(C_0), .valA1(A_1), .valC1(C_1), .Icode(Icode), .aluA_0(alua_1_alua_0),
    .aluA_1(alua_1_alua_1));
  aluB alub_1 (.ValB_0(B_0), .ValB_1(B_1), .icode(Icode), .aluB_0(alub_1_alub_0), .aluB_1(alub_1_alub_1));
  setCC setcc_1 (.Icode(Icode), .out_2(setcc_1_out_2));
  checkJM checkjm_1 (.ifun(ifun), .icode(Icode), .\output (checkjm_1_output));
  CondCode condcode_1 (
    .OF(condcode_1_of), .SF(condcode_1_sf), .ZF(condcode_1_zf), .setCC(setcc_1_out_2),
    .OF_star(n64bitalu_1_of), .SF_star(n64bitalu_1_sf), .ZF_star(n64bitalu_1_zf));
  _64bitALU u_64bitalu_1 (
    .A_0(alua_1_alua_0), .A_1(alua_1_alua_1), .B_0(alub_1_alub_0), .B_1(alub_1_alub_1), .Cin(1'b0),
    .ZF(n64bitalu_1_zf), .SF(n64bitalu_1_sf), .OF(n64bitalu_1_of), .in_5(alufun_1_ifunout),
    .output_0(valE_0), .output_1(valE_1));  // open: Cout
  aluFun alufun_1 (.ifunIn(ifun), .icode(Icode), .ifunOut(alufun_1_ifunout));
  cond cond_1 (.iFun(checkjm_1_output), .cond(Cond), .OF(condcode_1_of), .SF(condcode_1_sf), .ZF(condcode_1_zf));

  // Notes on the sheet:
  //   setCC
  //   aluFun
endmodule

module aluA (
  input  [31:0] valA0,
  input  [31:0] valC0,
  input  [31:0] valA1,
  input  [31:0] valC1,
  input  [3:0] Icode,
  output [31:0] aluA_0,
  output [31:0] aluA_1
);

  Multiplexer #(.select(4), .width(32), .enable("false")) multiplexer_1 (
    .in0({32{1'b0}}), .in1({32{1'b0}}), .in2(valA0), .in3(valC0), .in4(valC0), .in5(valC0), .in6(valA0),
    .in7({32{1'b0}}), .in8(32'hfffffff8), .in9(32'h8), .in10(32'hfffffff8), .in11(32'h8), .in12({32{1'b0}}),
    .in13({32{1'b0}}), .in14({32{1'b0}}), .in15({32{1'b0}}), .out(aluA_0), .sel(Icode));
  Multiplexer #(.select(4), .width(32), .enable("false")) multiplexer_2 (
    .in0({32{1'b0}}), .in1({32{1'b0}}), .in2(valA1), .in3(valC1), .in4(valC1), .in5(valC1), .in6(valA1),
    .in7({32{1'b0}}), .in8(32'hfffffff8), .in9(32'h8), .in10(32'hfffffff8), .in11(32'h8), .in12({32{1'b0}}),
    .in13({32{1'b0}}), .in14({32{1'b0}}), .in15({32{1'b0}}), .out(aluA_1), .sel(Icode));
endmodule

module setCC (
  input  [3:0] Icode,
  output out_2
);

  wire or_1_out, or_2_out, or_3_out, xor_1_out, xor_2_out, xor_3_out, xor_4_out;

  xor xor_1 (xor_1_out, Icode[0], 1'b0);
  xor xor_2 (xor_2_out, Icode[1], 1'b1);
  xor xor_3 (xor_3_out, Icode[2], 1'b1);
  xor xor_4 (xor_4_out, Icode[3], 1'b0);
  or or_1 (or_1_out, xor_1_out, xor_2_out);
  or or_2 (or_2_out, xor_3_out, xor_4_out);
  or or_3 (or_3_out, or_1_out, or_2_out);
  not not_1 (out_2, or_3_out);
endmodule

module aluB (
  input  [31:0] ValB_0,
  input  [31:0] ValB_1,
  input  [3:0] icode,
  output [31:0] aluB_0,
  output [31:0] aluB_1
);

  Multiplexer #(.select(4), .width(32), .enable("false")) multiplexer_1 (
    .in0({32{1'b0}}), .in1({32{1'b0}}), .in2({32{1'b0}}), .in3({32{1'b0}}), .in4(ValB_0), .in5(ValB_0),
    .in6(ValB_0), .in7({32{1'b0}}), .in8(ValB_0), .in9(ValB_0), .in10(ValB_0), .in11(ValB_0),
    .in12({32{1'b0}}), .in13({32{1'b0}}), .in14({32{1'b0}}), .in15({32{1'b0}}), .out(aluB_0), .sel(icode));
  Multiplexer #(.select(4), .width(32), .enable("false")) multiplexer_2 (
    .in0({32{1'b0}}), .in1({32{1'b0}}), .in2({32{1'b0}}), .in3({32{1'b0}}), .in4(ValB_1), .in5(ValB_1),
    .in6(ValB_1), .in7({32{1'b0}}), .in8(ValB_1), .in9(ValB_1), .in10(ValB_1), .in11(ValB_1),
    .in12({32{1'b0}}), .in13({32{1'b0}}), .in14({32{1'b0}}), .in15({32{1'b0}}), .out(aluB_1), .sel(icode));
endmodule

module memAddr (
  input  [31:0] valE_0,
  input  [31:0] valA_0,
  input  [31:0] valE_1,
  input  [31:0] valA_1,
  input  [3:0] Icode,
  output [31:0] memAdd_0,
  output [31:0] memAdd_1
);

  Multiplexer #(.select(4), .width(32), .enable("false")) multiplexer_1 (
    .in0({32{1'b0}}), .in1({32{1'b0}}), .in2({32{1'b0}}), .in3({32{1'b0}}), .in4(valE_0), .in5(valE_0),
    .in6({32{1'b0}}), .in7({32{1'b0}}), .in8(valE_0), .in9(valA_0), .in10(valE_0), .in11(valA_0),
    .in12({32{1'b0}}), .in13({32{1'b0}}), .in14({32{1'b0}}), .in15({32{1'b0}}), .out(memAdd_0), .sel(Icode));
  Multiplexer #(.select(4), .width(32), .enable("false")) multiplexer_2 (
    .in0({32{1'b0}}), .in1({32{1'b0}}), .in2({32{1'b0}}), .in3({32{1'b0}}), .in4(valE_1), .in5(valE_1),
    .in6({32{1'b0}}), .in7({32{1'b0}}), .in8(valE_1), .in9(valA_1), .in10(valE_1), .in11(valA_1),
    .in12({32{1'b0}}), .in13({32{1'b0}}), .in14({32{1'b0}}), .in15({32{1'b0}}), .out(memAdd_1), .sel(Icode));
endmodule

module aluFun (
  input  [3:0] ifunIn,
  input  [3:0] icode,
  output [3:0] ifunOut
);

  Multiplexer #(.select(4), .width(4), .enable("false")) multiplexer_1 (
    .in0(4'b0000), .in1(4'b0000), .in2(4'b0000), .in3(4'b0000), .in4(4'b0000), .in5(4'b0000), .in6(ifunIn),
    .in7(4'b0000), .in8(4'b0000), .in9(4'b0000), .in10(4'b0000), .in11(4'b0000), .in12(4'b0000),
    .in13(4'b0000), .in14(4'b0000), .in15(4'b0000), .out(ifunOut), .sel(icode));
endmodule

module memData (
  input  [31:0] valA_0,
  input  [31:0] valP_0,
  input  [31:0] valA_1,
  input  [3:0] Icode,
  output [31:0] memData_0,
  output [31:0] memData_1
);

  Multiplexer #(.select(4), .width(32), .enable("false")) multiplexer_1 (
    .in0({32{1'b0}}), .in1({32{1'b0}}), .in2({32{1'b0}}), .in3({32{1'b0}}), .in4(valA_0), .in5({32{1'b0}}),
    .in6({32{1'b0}}), .in7({32{1'b0}}), .in8(valP_0), .in9({32{1'b0}}), .in10(valA_0), .in11({32{1'b0}}),
    .in12({32{1'b0}}), .in13({32{1'b0}}), .in14({32{1'b0}}), .in15({32{1'b0}}), .out(memData_0), .sel(Icode));
  Multiplexer #(.select(4), .width(32), .enable("false")) multiplexer_2 (
    .in0({32{1'b0}}), .in1({32{1'b0}}), .in2({32{1'b0}}), .in3({32{1'b0}}), .in4(valA_1), .in5({32{1'b0}}),
    .in6({32{1'b0}}), .in7({32{1'b0}}), .in8({32{1'b0}}), .in9({32{1'b0}}), .in10(valA_1), .in11({32{1'b0}}),
    .in12({32{1'b0}}), .in13({32{1'b0}}), .in14({32{1'b0}}), .in15({32{1'b0}}), .out(memData_1), .sel(Icode));
endmodule

module Memory (
  input  [31:0] valE_0,
  input  [31:0] valE_1,
  input  [31:0] valA_0,
  input  DataClear,
  input  [31:0] valA_1,
  input  Clock,
  input  [31:0] valP_0,
  input  imemError,
  input  insValid,
  input  [3:0] Icode,
  output [31:0] valM_1,
  output [31:0] valM_0,
  output [1:0] statusCode
);

  wire dmem_1_p7, memread_1_out_2, memwrite_1_out_2;
  wire [31:0] memaddr_1_memadd_0, memaddr_1_memadd_1, memdata_1_memdata_0, memdata_1_memdata_1;

  memAddr memaddr_1 (
    .valE_0(valE_0), .valA_0(valA_0), .valE_1(valE_1), .valA_1(valA_1), .Icode(Icode),
    .memAdd_0(memaddr_1_memadd_0), .memAdd_1(memaddr_1_memadd_1));
  memData memdata_1 (
    .valA_0(valA_0), .valP_0(valP_0), .valA_1(valA_1), .Icode(Icode), .memData_0(memdata_1_memdata_0),
    .memData_1(memdata_1_memdata_1));
  memRead memread_1 (.icode(Icode), .out_2(memread_1_out_2));
  memWrite memwrite_1 (.icode(Icode), .out_2(memwrite_1_out_2));
  // dmem dmem_1: pin names not known; wires that end beside it: memaddr_1_memadd_1, memaddr_1_memadd_0, memdata_1_memdata_1, memdata_1_memdata_0, memread_1_out_2, memwrite_1_out_2, dmem_1_p7, Clock, DataClear, valM_1, valM_0
  Stat stat_1 (.insValid(insValid), .dmemerror(dmem_1_p7), .imem_error(imemError), .icode(Icode), .Output(statusCode));

  // Notes on the sheet:
  //   memData
  //   memAddr
endmodule

module memRead (
  input  [3:0] icode,
  output out_2
);

  Multiplexer #(.select(4), .enable("false")) multiplexer_1 (
    .in0(1'b0), .in1(1'b0), .in2(1'b0), .in3(1'b0), .in4(1'b0), .in5(1'b1), .in6(1'b0), .in7(1'b0),
    .in8(1'b0), .in9(1'b1), .in10(1'b0), .in11(1'b1), .in12(1'b0), .in13(1'b0), .in14(1'b0), .in15(1'b0),
    .out(out_2), .sel(icode));
endmodule

module memWrite (
  input  [3:0] icode,
  output out_2
);

  Multiplexer #(.select(4), .enable("false")) multiplexer_1 (
    .in0(1'b0), .in1(1'b0), .in2(1'b0), .in3(1'b0), .in4(1'b1), .in5(1'b0), .in6(1'b0), .in7(1'b0),
    .in8(1'b1), .in9(1'b0), .in10(1'b1), .in11(1'b0), .in12(1'b0), .in13(1'b0), .in14(1'b0), .in15(1'b0),
    .out(out_2), .sel(icode));
endmodule

module Stat (
  input  insValid,
  input  dmemerror,
  input  imem_error,
  input  [3:0] icode,
  output [1:0] Output
);

  wire or_2_out, or_3_out, or_4_out, xor_1_out, xor_2_out, xor_3_out, xor_4_out;
  wire [2:0] not_1_out;

  not not_1 (not_1_out[0], insValid);
  or or_1 (not_1_out[1], dmemerror, imem_error);
  xor xor_1 (xor_1_out, icode[0], 1'b0);
  xor xor_2 (xor_2_out, icode[1], 1'b0);
  xor xor_3 (xor_3_out, icode[2], 1'b0);
  xor xor_4 (xor_4_out, icode[3], 1'b0);
  or or_2 (or_2_out, xor_1_out, xor_2_out);
  or or_3 (or_3_out, xor_3_out, xor_4_out);
  or or_4 (or_4_out, or_2_out, or_3_out);
  not not_2 (not_1_out[2], or_4_out);
  Multiplexer #(.select(3), .width(2), .enable("false")) multiplexer_1 (
    .in0(2'b00), .in1(2'b01), .in2(2'b10), .in3(2'b01), .in4(2'b11), .in5(2'b11), .in6(2'b11), .in7(2'b11),
    .out(Output), .sel(not_1_out));
endmodule

module CondCode (
  input  OF_star,
  input  SF_star,
  input  ZF_star,
  input  setCC,
  output OF,
  output SF,
  output ZF
);

  Register #(.width(1), .trigger("high")) OF_reg (.D(OF_star), .Q(OF), .clk(setCC));  // open: en, clr
  Register #(.width(1), .trigger("high")) SF_reg (.D(SF_star), .Q(SF), .clk(setCC));  // open: en, clr
  Register #(.width(1), .trigger("high")) ZF_reg (.D(ZF_star), .Q(ZF), .clk(setCC));  // open: en, clr
endmodule

module cond (
  input  OF,
  input  SF,
  input  ZF,
  input  [3:0] iFun,
  output cond
);

  wire and_1_out, and_2_out, and_3_out, and_4_out, and_5_out, and_6_out, and_7_out, or_1_out, xor_1_out,
       xor_2_out;

  and and_1 (and_1_out, 1'b1, ZF);
  xor xor_1 (xor_1_out, SF, OF);
  and and_2 (and_2_out, 1'b0, ZF);
  and and_3 (and_3_out, SF, OF);
  or or_1 (or_1_out, and_1_out, xor_1_out);
  and and_4 (and_4_out, and_2_out, and_3_out);
  and and_5 (and_5_out, 1'b1, ZF);
  xor xor_2 (xor_2_out, OF, SF);
  and and_6 (and_6_out, 1'b0, ZF);
  and and_7 (and_7_out, SF, OF);
  Multiplexer #(.select(4), .enable("false")) multiplexer_1 (
    .in0(1'b0), .in1(or_1_out), .in2(xor_2_out), .in3(and_5_out), .in4(and_6_out), .in5(and_7_out),
    .in6(and_4_out), .in7(1'b0), .in8(1'b0), .in9(1'b0), .in10(1'b0), .in11(1'b0), .in12(1'b0), .in13(1'b0),
    .in14(1'b0), .in15(1'b0), .out(cond), .sel(iFun));
endmodule

module checkJM (
  input  [3:0] ifun,
  input  [3:0] icode,
  output [3:0] \output 
);

  Multiplexer #(.select(4), .width(4), .enable("false")) multiplexer_1 (
    .in0(4'b0001), .in1(4'b0001), .in2(ifun), .in3(4'b0001), .in4(4'b0001), .in5(4'b0001), .in6(4'b0001),
    .in7(ifun), .in8(4'b0001), .in9(4'b0001), .in10(4'b0001), .in11(4'b0001), .in12(4'b0001), .in13(4'b0001),
    .in14(4'b0001), .in15(4'b0001), .out(\output ), .sel(icode));
endmodule
