// Logisim project y86.circ as structural Verilog: 13 circuits, main circuit Align
module main (
  input  Reset
);

  wire and_1_out, Clock_out, cnd, imemError, instrValid, nor_1_out, not_1_out;
  wire [1:0] Stat_q, statusCode;
  wire [3:0] fetch_1_ra, fetch_1_rb, icode, ifun;
  wire [7:0] imem_1_p3, imem_1_p4, imem_1_p5, imem_1_p6, imem_1_p7, imem_1_p8, imem_1_p9, imem_1_p10,
       imem_1_p11, imem_1_p12;
  wire [31:0] PC, PChold_q, undriven, valA_0, valA_1, valB_0, valB_1, valC_0, valC_1, valE_0, valE_1, valM_0,
       valM_1, valP;

  and and_1 (and_1_out, Clock_out, nor_1_out);
  Clock Clock (.out(Clock_out));
  Register #(.width(32)) u_PC (.D(PChold_q), .Q(PC), .clk(and_1_out), .clr(Reset));  // open: en
  nor nor_1 (nor_1_out, Stat_q[1], Stat_q[0]);
  not not_1 (not_1_out, and_1_out);
  Register #(.width(2)) Stat (.D(statusCode), .Q(Stat_q), .clk(not_1_out));  // open: en, clr
  // imem imem_1: pin names not known; wires that end beside it: PC, imemError, imem_1_p3, imem_1_p4, imem_1_p5, imem_1_p6, imem_1_p7, imem_1_p8, imem_1_p9, imem_1_p10, imem_1_p11, imem_1_p12
  Fetch fetch_1 (
    .in_1(imem_1_p3), .in_2(imem_1_p4), .in_3(imem_1_p5), .in_4(imem_1_p6), .in_5(imem_1_p7),
    .in_6(imem_1_p8), .in_7(imem_1_p9), .in_8(imem_1_p10), .in_9(imem_1_p11), .in_10(imem_1_p12),
    .icode(icode), .ifun(ifun), .PC(PC), .valP(valP), .rA(fetch_1_ra), .rB(fetch_1_rb), .valC1(valC_0),
    .valC2(valC_1), .validInstuction(instrValid));
  Decode decode_1 (
    .icode(icode), .rA(fetch_1_ra), .rB(fetch_1_rb), .cnd(cnd), .valA_1(valA_1), .valA_0(valA_0),
    .valB_1(valB_1), .valB_0(valB_0), .valM0(valM_0), .valM1(valM_1), .valE0(valE_0), .valE1(valE_1));
  PCupdate pcupdate_1 (.valP(valP), .cnd(cnd), .valC_0(valC_0), .valM_0(valM_0), .icode(icode), .NewPC(undriven));
  Execute execute_1 (
    .A_0(valA_0), .C_0(valC_0), .A_1(valA_1), .C_1(valC_1), .B_0(valB_0), .B_1(valB_1), .Cond(cnd),
    .Icode(icode), .ifun(ifun), .valE_0(valE_0), .valE_1(valE_1));
  Memory memory_1 (
    .valE_0(valE_0), .valE_1(valE_1), .valA_0(valA_0), .valA_1(valA_1), .valP_0(valP), .Icode(icode),
    .Clock(not_1_out), .DataClear(Reset), .insValid(instrValid), .imemError(imemError), .valM_1(valM_1),
    .valM_0(valM_0), .statusCode(statusCode));
  Register #(.width(32)) PChold (.D(undriven), .en(1'b1), .Q(PChold_q), .clk(not_1_out), .clr(Reset));
endmodule

module Align (
  input  [7:0] B1,
  input  [7:0] B2,
  input  [7:0] B3,
  input  [7:0] B4,
  input  [7:0] B5,
  input  [7:0] B6,
  input  [7:0] B7,
  input  [7:0] B8,
  input  NeedRegs,
  input  [7:0] B9,
  output [3:0] rA,
  output [3:0] rB,
  output [31:0] valC_0,
  output [31:0] valC_1
);

  Multiplexer #(.width(32), .enable("false")) multiplexer_1 (
    .in0({B4, B3, B2, B1}), .in1({B5, B4, B3, B2}), .out(valC_0), .sel(NeedRegs));
  Multiplexer #(.width(32), .enable("false")) multiplexer_2 (
    .in0({B8, B7, B6, B5}), .in1({B9, B8, B7, B6}), .out(valC_1), .sel(NeedRegs));

  assign rA = B1[3:0];
  assign rB = B1[7:4];
endmodule

module Fetch (
  input  [7:0] in_1,
  input  [7:0] in_2,
  input  [7:0] in_3,
  input  [7:0] in_4,
  input  [7:0] in_5,
  input  [7:0] in_6,
  input  [7:0] in_7,
  input  [7:0] in_8,
  input  [7:0] in_9,
  input  [7:0] in_10,
  input  [31:0] PC,
  output validInstuction,
  output [3:0] icode,
  output [3:0] ifun,
  output [3:0] rA,
  output [3:0] rB,
  output [31:0] valC1,
  output [31:0] valC2,
  output [31:0] valP
);

  wire needreg_1_needreg, needvalc_1_needsvalc;

  needValC needvalc_1 (.icode(in_1[3:0]), .needsValC(needvalc_1_needsvalc));
  needReg needreg_1 (.icode(in_1[3:0]), .needReg(needreg_1_needreg));
  Align align_1 (
    .B1(in_2), .B2(in_3), .B3(in_4), .B4(in_5), .B5(in_6), .B6(in_7), .B7(in_8), .B8(in_9), .B9(in_10),
    .rA(rA), .rB(rB), .valC_0(valC1), .NeedRegs(needreg_1_needreg), .valC_1(valC2));
  instrValid instrvalid_1 (.in_1(in_1[3:0]), .out_2(validInstuction));
  PC_Increment pc_increment_1 (.NeedReg(needreg_1_needreg), .ValC(needvalc_1_needsvalc), .PC(PC), .valP(valP));

  assign icode = in_1[3:0];
  assign ifun = in_1[7:4];
endmodule

module needReg (
  input  [3:0] icode,
  output needReg
);

  Multiplexer #(.select(4), .disabled(0), .enable("false")) multiplexer_1 (
    .in0(1'b0), .in1(1'b0), .in2(1'b1), .in3(1'b1), .in4(1'b1), .in5(1'b1), .in6(1'b1), .in7(1'b0),
    .in8(1'b0), .in9(1'b0), .in10(1'b1), .in11(1'b1), .in12(1'b0), .in13(1'b0), .in14(1'b0), .in15(1'b0),
    .out(needReg), .sel(icode));
endmodule

module needValC (
  input  [3:0] icode,
  output needsValC
);

  Multiplexer #(.select(4), .enable("false")) multiplexer_1 (
    .in0(1'b0), .in1(1'b0), .in2(1'b0), .in3(1'b0), .in4(1'b1), .in5(1'b1), .in6(1'b1), .in7(1'b0),
    .in8(1'b1), .in9(1'b1), .in10(1'b0), .in11(1'b0), .in12(1'b0), .out(needsValC), .sel(icode));  // open: in13, in14, in15
endmodule

module PC_Increment (
  input  NeedReg,
  input  ValC,
  input  [31:0] PC,
  output [31:0] valP
);

  wire [0:0] not_1_out;

  not not_1 (not_1_out[0], NeedReg);
  _32bitALU u_32bitalu_1 (
    .A({{28{1'b0}}, ValC, 1'b0, NeedReg, not_1_out[0]}), .B(PC), .Cin(1'b0), .in_4(4'b0000), .out_8(valP));  // open: Cout, OF, ZF, SF
endmodule

module Decode (
  input  [31:0] valM0,
  input  [31:0] valM1,
  input  [31:0] valE0,
  input  [31:0] valE1,
  input  [3:0] icode,
  input  [3:0] rA,
  input  [3:0] rB,
  input  cnd,
  output [31:0] valA_1,
  output [31:0] valA_0,
  output [31:0] valB_1,
  output [31:0] valB_0
);

  wire [3:0] dste_1_srca, dstm_1_srca, srca_1_srca, srcb_1_srca;

  srcA srca_1 (.rA(rA), .icode(icode), .srcA(srca_1_srca));
  srcB srcb_1 (.rB(rB), .icode(icode), .srcA(srcb_1_srca));
  dstE dste_1 (.cnd(cnd), .rB(rB), .icode(icode), .srcA(dste_1_srca));
  dstM dstm_1 (.rA(rA), .icode(icode), .srcA(dstm_1_srca));
  // regfile regfile_1: pin names not known; wires that end beside it: srca_1_srca, srcb_1_srca, dste_1_srca, valE1, valE0, dstm_1_srca, valM1, valM0, valA_1, valA_0, valB_1, valB_0

  // Other names for the same wires on the sheet: e_0[31:0] = valE0; e_1[31:0] = valE1; m_0[31:0] = valM0;
  //   m_1[31:0] = valM1
endmodule

module instrValid (
  input  [3:0] in_1,
  output out_2
);

  Multiplexer #(.select(4), .enable("false")) multiplexer_1 (
    .in0(1'b1), .in1(1'b1), .in2(1'b1), .in3(1'b1), .in4(1'b1), .in5(1'b1), .in6(1'b1), .in7(1'b1),
    .in8(1'b1), .in9(1'b1), .in10(1'b1), .in11(1'b1), .in12(1'b0), .in13(1'b0), .in14(1'b0), .in15(1'b0),
    .out(out_2), .sel(in_1));
endmodule

module srcA (
  input  [3:0] rA,
  input  [3:0] icode,
  output [3:0] srcA
);

  Multiplexer #(.select(4), .width(4), .enable("false")) multiplexer_1 (
    .in0(4'b1111), .in1(4'b1111), .in2(rA), .in3(4'b1111), .in4(rA), .in5(4'b1111), .in6(rA), .in7(4'b1111),
    .in8(4'b1111), .in9(4'b0100), .in10(rA), .in11(4'b0100), .in12(4'b1111), .in13(4'b1111), .in14(4'b1111),
    .in15(4'b1111), .out(srcA), .sel(icode));
endmodule

module srcB (
  input  [3:0] rB,
  input  [3:0] icode,
  output [3:0] srcA
);

  Multiplexer #(.select(4), .width(4), .enable("false")) multiplexer_1 (
    .in0(4'b1111), .in1(4'b1111), .in2(4'b1111), .in3(4'b1111), .in4(rB), .in5(rB), .in6(rB), .in7(4'b1111),
    .in8(4'b0100), .in9(4'b0100), .in10(4'b0100), .in11(4'b0100), .in12(4'b1111), .in13(4'b1111),
    .in14(4'b1111), .in15(4'b1111), .out(srcA), .sel(icode));
endmodule

module dstE (
  input  cnd,
  input  [3:0] rB,
  input  [3:0] icode,
  output [3:0] srcA
);

  wire [3:0] and_1_out;

  assign and_1_out = {4{cnd}} & rB;  // AND_Gate and_1, 4 bits wide
  Multiplexer #(.select(4), .width(4), .enable("false")) multiplexer_1 (
    .in0(4'b1111), .in1(4'b1111), .in2(and_1_out), .in3(rB), .in4(4'b1111), .in5(4'b1111), .in6(rB),
    .in7(4'b1111), .in8(4'b0100), .in9(4'b0100), .in10(4'b0100), .in11(4'b0100), .in12(4'b1111),
    .in13(4'b1111), .in14(4'b1111), .in15(4'b1111), .out(srcA), .sel(icode));
endmodule

module dstM (
  input  [3:0] rA,
  input  [3:0] icode,
  output [3:0] srcA
);

  Multiplexer #(.select(4), .width(4), .enable("false")) multiplexer_1 (
    .in0(4'b1111), .in1(4'b1111), .in2(4'b1111), .in3(4'b1111), .in4(4'b1111), .in5(rA), .in6(4'b1111),
    .in7(4'b1111), .in8(4'b1111), .in9(4'b1111), .in10(4'b1111), .in11(rA), .in12(4'b1111), .in13(4'b1111),
    .in14(4'b1111), .in15(4'b1111), .out(srcA), .sel(icode));
endmodule

module PCupdate (
  input  [31:0] valP,
  input  cnd,
  input  [31:0] valC_0,
  input  [31:0] NewPC,
  input  [31:0] valM_0,
  input  [3:0] icode
);

  wire [31:0] multiplexer_1_out;

  Multiplexer #(.width(32), .enable("false")) multiplexer_1 (
    .in0(valP), .in1(valC_0), .out(multiplexer_1_out), .sel(cnd));
  Multiplexer #(.select(4), .width(32), .enable("false")) multiplexer_2 (
    .in0(valP), .in1(valP), .in2(valP), .in3(valP), .in4(valP), .in5(valP), .in6(valP),
    .in7(multiplexer_1_out), .in8(valC_0), .in9(valM_0), .in10(valP), .in11(valP), .in12(valP), .in13(valP),
    .in14(valP), .in15(valP), .out(NewPC), .sel(icode));
endmodule
